// Logisim project runner.circ as structural Verilog: 1 circuit, main circuit main
module main (
  output [7:0] r0,
  output [7:0] r1,
  output [7:0] r2,
  output [7:0] r3,
  output [15:0] pc,
  output [7:0] sp,
  output [7:0] ps,
  output halt
);

  wire cdm_8_mark5_1_p10, cdm_8_mark5_1_p11, cdm_8_mark5_1_p12, clock_1_out, decoder_1_out0, decoder_1_out1,
       not_1_out;
  wire [7:0] cdm_8_mark5_1_p14, cdm_8_mark5_1_p15, controlled_buffer_1_out;
  wire [15:0] cdm_8_mark5_1_p13;

  Clock clock_1 (.out(clock_1_out));
  // CdM_8_mark5 cdm_8_mark5_1: pin names not known; wires that end beside it: r0, r1, clock_1_out, r2, r3, halt, pc, sp, ps, cdm_8_mark5_1_p10, cdm_8_mark5_1_p11, cdm_8_mark5_1_p12, cdm_8_mark5_1_p13, cdm_8_mark5_1_p14, cdm_8_mark5_1_p15
  Decoder #(.disabled(0)) decoder_1 (
    .out0(decoder_1_out0), .out1(decoder_1_out1), .sel(cdm_8_mark5_1_p10), .en(cdm_8_mark5_1_p11));
  not not_1 (not_1_out, cdm_8_mark5_1_p12);
  assign controlled_buffer_1_out = not_1_out ? cdm_8_mark5_1_p14 : 8'bz;  // Controlled_Buffer controlled_buffer_1
  assign cdm_8_mark5_1_p15 = cdm_8_mark5_1_p12 ? controlled_buffer_1_out : 8'bz;  // Controlled_Buffer controlled_buffer_2
  ROM #(.addrWidth(16)) rom_1 (.addr(cdm_8_mark5_1_p13), .data(controlled_buffer_1_out), .sel(decoder_1_out0));
  RAM ram_1 (
    .addr(cdm_8_mark5_1_p13[7:0]), .data(controlled_buffer_1_out), .sel(decoder_1_out1), .clk(clock_1_out),
    .ld(cdm_8_mark5_1_p12));  // open: clr

  // Notes on the sheet:
  //   contents of rom_1 (hex, n*v repeats v):
  //   d0 1 c0 d0 0 c0 d0 80 c0 d9 48 6f 77 20 64 61 72 65 20 79 6f 75 20 69 6e 74 65 72 72 75 70 74 20 6d
  //   65 a 0 43 61 6c 63 75 6c 61 74 69 6e 67 20 72 30 20 66 69 62 20 6e 75 6d 62 65 72 a 0 44 6f 6e 65 2c
  //   20 79 6f 75 72 20 61 6e 73 77 65 72 20 69 6e 20 72 30 a 0 59 6f 75 20 61 63 74 69 76 61 74 65 64 20
  //   66 69 72 73 74 20 76 65 63 74 6f 72 a 140*0 d0 25 d6 12 1 d0 5 d6 23 1 c0 d0 40 d6 12 1 c4 d4 c0 c1
  //   c2 d2 0 f1 5 e0 5 a9 8c ee f9 c6 c5 c4 d7 c3 d3 2 73 eb 10 88 c0 d6 23 1 3 c4 88 c0 d6 23 1 13 c4 c
  //   c7 d7 61637*0 c0 d0 59 d6 12 1 c4 d9 247*0 c0 d0 a d6 12 1 c4 d9 3290*0 ff f1 0 0 fe f2
endmodule
